# Fritzing sketch apds9960_bb (saved by Fritzing 0.9.3b)
circuit board: 8.46667cm x 5.64444cm
stripboards: 1

parts:
  J1 = shrouded pin header, 26 pins [form="♂ (shrouded male)"]
  J5 = male pin header, 5 pins [form="♂ (male)"]
  J6 = male pin header, 7 pins [form="♂ (male)"]
  J4 = male pin header, 3 pins [form="♂ (male)"]
  J3 = male pin header, 4 pins [form="♂ (male)"]

nets (from the pcb view):
  N1: J1.pin1, J5.pin1, J6.pin6, J3.pin1
  N2: J1.pin2, J5.pin4, J3.pin4
  N3: J1.pin3, J5.pin3, J3.pin3
  N4: J1.pin10, J6.pin4
  N5: J1.pin12, J6.pin5
  N6: J1.pin15, J6.pin1
  N7: J1.pin16, J6.pin3
  N8: J1.pin18, J6.pin2
  N9: J1.pin21, J5.pin5
  N10: J1.pin22, J4.pin3
  N11: J1.pin23, J4.pin2
  N12: J1.pin24, J6.pin7, J4.pin1
  N13: J5.pin2, J3.pin2
